# Fritzing sketch cam_sketch (saved by Fritzing 0.9.4)
breadboards: 1

parts:
  ESP32_-_Back1 = ESP32 - CAM
  Part1 = FTDI Basic Programmer
  R1 = Resistor [tolerance=±5% resistance=10k package="1206 [SMD]"]
  J1 = Piezo Speaker
  S1 = Round Pushbutton

nets:
  N1: ESP32_-_Back1.GPIO2, J1.pin2
  N2: ESP32_-_Back1.GPIO12, R1.Pin_0
  N3: ESP32_-_Back1.5V, Part1.POWER, R1.Pin_1, S1.leg0
  N4: ESP32_-_Back1.GPIO3_/_RX, Part1.TXO
  N5: ESP32_-_Back1.GPIO1_/_TX, Part1.RXI
  N6: ESP32_-_Back1.GND#16, Part1.GND, J1.pin1, S1.leg1

custom parts:
  ESP32 - CAM: The ESP32-CAM has a very competitive small-size camera module that can operate independently as a minimum system with a footprint of only 27*40.5*4.5mm and a deep sleep current of up to 6mA.
